// Logisim project Lab1DD1.circ as structural Verilog: 1 circuit, main circuit main
module main (
  input  A,
  input  B,
  input  C,
  output X,
  output Y
);

  wire n7402_1_p1, n7402_1_p4, n7408_1_p3, n7408_1_p6, n7408_1_p11, n7408_1_p14;

  // _7402 7402_1: pin names not known; wires that end beside it: n7402_1_p1, A, A, n7402_1_p4, C, C, 1'b0, 1'b1
  // _7408 7408_1: pin names not known; wires that end beside it: A, C, n7408_1_p3, n7402_1_p1, B, n7408_1_p6, 1'b0, 1'b1, n7402_1_p1, n7402_1_p4, n7408_1_p11, n7402_1_p4, B, n7408_1_p14
  // _7432 7432_1: pin names not known; wires that end beside it: n7408_1_p3, n7408_1_p6, X, n7408_1_p11, n7408_1_p14, Y, 1'b0, 1'b1

  // Notes on the sheet:
  //   NOR
  //   AND
  //   OR
endmodule
