// Logisim project 4x16 Decoder.circ as structural Verilog: 1 circuit, main circuit main
module main (
  input  C,
  input  D,
  input  A,
  input  B,
  output out_5,
  output out_6,
  output out_7,
  output out_8,
  output out_9,
  output out_10,
  output out_11,
  output out_12,
  output out_13,
  output out_14,
  output out_15,
  output out_16,
  output out_17,
  output out_18,
  output out_19,
  output out_20
);

  wire n74139_1_p3, n74139_1_p4, n74139_1_p5, n74139_1_p6;

  // _74139 74139_1: pin names not known; wires that end beside it: A, B, n74139_1_p3, n74139_1_p4, n74139_1_p5, n74139_1_p6, 1'b0, 1'b1
  // _74139 74139_2: pin names not known; wires that end beside it: n74139_1_p3, C, D, out_5, out_6, out_7, out_8, 1'b0, 1'b1, n74139_1_p4, C, D, out_9, out_10, out_11, out_12
  // _74139 74139_3: pin names not known; wires that end beside it: n74139_1_p5, C, D, out_13, out_14, out_15, out_16, 1'b0, 1'b1, n74139_1_p6, C, D, out_17, out_18, out_19, out_20
endmodule
