// Logisim project template7400.circ as structural Verilog: 1 circuit, main circuit main
module main (
  input  S,
  input  A,
  input  B,
  output o1,
  output o2
);

  wire n74157_1_p4;

  // _74157 74157_1: pin names not known; wires that end beside it: S, A, B, n74157_1_p4, 1'b0, 1'b1
  // _7408 7408_1: pin names not known; wires that end beside it: A, n74157_1_p4, o1, 1'b0, 1'b1
  // _7486 7486_1: pin names not known; wires that end beside it: B, n74157_1_p4, o2, 1'b0, 1'b1
endmodule
