// Logisim project PreLab2.circ as structural Verilog: 1 circuit, main circuit main
module main (
  input  A,
  output X
);

  wire n7408_1_p3, n7408_1_p6, n7408_1_p9, n7408_1_p11;

  // _7408 7408_1: pin names not known; wires that end beside it: A, A, n7408_1_p3, n7408_1_p3, n7408_1_p3, n7408_1_p6, 1'b0, 1'b1, n7408_1_p9, n7408_1_p9, n7408_1_p11, n7408_1_p6, n7408_1_p6, n7408_1_p9
  // _7408 7408_2: pin names not known; wires that end beside it: A, n7408_1_p11, X, 1'b0, 1'b1
endmodule
